// Logisim project Project4.circ as structural Verilog: 16 circuits, main circuit main
module main (
  input  Reset
);

  wire ALUSrc, B, BL, Bx, CLK, control_unit_1_flagwrite, decoder_1_out0, decoder_1_out1, decoder_1_out2,
       decoder_1_out3, MemtoReg, MemW, RegW;
  wire [1:0] ALUControl, ImmdSrc, RegSrc;
  wire [3:0] ALUFlags, IW_Help__3_0, IW_Help__15_12, IW_Help__19_16, multiplexer_2_out, multiplexer_3_out,
       multiplexer_4_out;
  wire [23:0] IW_Help__23_0;
  wire [31:0] adder_1_out, adder_2_out, alu_1_result, Data_Memory_rd, Extender_output, IW, IW_Help_iw_2,
       multiplexer_1_out, multiplexer_5_out, multiplexer_6_out, PC, R0, R1, R2, R3, R4, R5, R6, R7, R8, R9,
       R10, R11, R12, R13, R14, Register_File_rd1, Register_File_rd2, Result;

  Decoder_part #(.select(2), .disabled(0), .enable("false")) decoder_1 (
    .out0(decoder_1_out0), .out1(decoder_1_out1), .out2(decoder_1_out2), .out3(decoder_1_out3),
    .sel(ALUControl));
  // Probe on ALUControl
  PC u_PC (.D(multiplexer_1_out), .Clock(CLK), .Output(PC), .Clear(Reset));
  Multiplexer #(.width(32), .disabled(0), .enable("false")) multiplexer_1 (
    .in0(adder_1_out), .in1(Result), .out(multiplexer_1_out), .sel(B));
  LED ADD (.in(decoder_1_out0));
  LED SUB (.in(decoder_1_out1));
  LED CMP (.in(decoder_1_out2));
  LED MOV (.in(decoder_1_out3));
  Instruction_Memory InstructionMem (.A(PC), .RD(IW));
  Adder #(.width(32)) adder_1 (.a(PC), .b(32'h4), .out(adder_1_out), .cin(1'b0));  // open: cout
  // Probe on ALUFlags
  // Probe on IW
  Inst_Word IW_Help (
    .IW(IW), .IW_2(IW_Help_iw_2), ._19_16(IW_Help__19_16), ._3_0(IW_Help__3_0), ._15_12(IW_Help__15_12),
    ._23_0(IW_Help__23_0));
  LED Branch_Exchange (.in(Bx));
  LED Branch_Link (.in(BL));
  LED Branch__Any (.in(B));
  // Probe on Result
  Multiplexer #(.width(4), .disabled(0), .enable("false")) multiplexer_2 (
    .in0(IW_Help__19_16), .in1(4'b1111), .out(multiplexer_2_out), .sel(RegSrc[0]));
  Multiplexer #(.width(4), .disabled(0), .enable("false")) multiplexer_3 (
    .in0(IW_Help__3_0), .in1(IW_Help__15_12), .out(multiplexer_3_out), .sel(RegSrc[1]));
  Multiplexer #(.width(4), .disabled(0), .enable("false")) multiplexer_4 (
    .in0(IW_Help__15_12), .in1(4'b1110), .out(multiplexer_4_out), .sel(BL));
  Adder #(.width(32)) adder_2 (.a(32'h4), .b(adder_1_out), .out(adder_2_out), .cin(1'b0));  // open: cout
  Multiplexer #(.width(32), .disabled(0), .enable("false")) multiplexer_5 (
    .in0(Result), .in1(adder_1_out), .out(multiplexer_5_out), .sel(BL));
  // Probe on PC
  Extender Extender (.Input(IW_Help__23_0), .in_1(ImmdSrc), .Output(Extender_output));
  Clock clock_1 (.out(CLK));
  // Probe on R14
  Control_Unit control_unit_1 (
    .Instruction_word(IW_Help_iw_2), .ALUFlags(ALUFlags), .MemtoReg(MemtoReg), .ALUSrc(ALUSrc),
    .ImmedSrc(ImmdSrc), .RegSrc({BL, RegSrc}), .ALUControl(ALUControl), .PCSrc(B), .RegW(RegW), .MemW(MemW),
    .FlagWrite(control_unit_1_flagwrite), .Clock(CLK), .BX(Bx));
  Register_File Register_File (
    .A1(multiplexer_2_out), .A2(multiplexer_3_out), .A3(multiplexer_4_out), .WD3(multiplexer_5_out),
    .R15(adder_2_out), .RD1(Register_File_rd1), .RD2(Register_File_rd2), .Clock(CLK), .WriteEnable(RegW),
    .Clear(Reset), .R14(R14), .R13(R13), .R12(R12), .R11(R11), .R10(R10), .R9(R9), .R8(R8), .R7(R7), .R6(R6),
    .R5(R5), .R4(R4), .R3(R3), .R2(R2), .R1(R1), .R0(R0));
  // Probe on Extender_output
  // Probe on R13
  // Probe on control_unit_1_flagwrite
  // Probe on R12
  ALU alu_1 (
    .A(Register_File_rd1), .B(multiplexer_6_out), .ALUControll(ALUControl), .RESULT(alu_1_result),
    .Flags(ALUFlags), .BL(BL), .Bx(Bx));
  Multiplexer #(.width(32), .disabled(0), .enable("false")) multiplexer_6 (
    .in0(Register_File_rd2), .in1(Extender_output), .out(multiplexer_6_out), .sel(ALUSrc));
  // Probe on R5
  // Probe on R3
  // Probe on R4
  // Probe on R2
  Data_Memory Data_Memory (
    .Clock(CLK), .WE(MemW), .RESET(Reset), .A(alu_1_result), .WD(Register_File_rd2), .RD(Data_Memory_rd));
  // Probe on R1
  Multiplexer #(.width(32), .disabled(0), .enable("false")) multiplexer_7 (
    .in0(alu_1_result), .in1(Data_Memory_rd), .out(Result), .sel(MemtoReg));
  // Probe on R0

  // Other names for the same wires on the sheet: PcSrc = B; RegSrc[2] = BL
endmodule

module Instruction_Memory (
  input  [31:0] A,
  output [31:0] RD
);

  // Probe on A
  ROM #(.dataWidth(32)) rom_1 (.addr(A[9:2]), .data(RD), .sel(1'b1));
  // Probe on RD

  // Notes on the sheet:
  //   contents of rom_1 (hex, n*v repeats v):
  //   e3a0d080 e08dd00d e08dd00d e3a0000a eb000000 eafffffe e24dd004 e58d4000 e24dd004 e58d5000 e24dd004
  //   e58de000 e3500000 a000008 e3500001 a000006 e1a04000 e2400001 ebfffff2 e1a05000 e2440002 ebffffef
  //   e0800005 e59de000 e28dd004 e59d5000 e28dd004 e59d4000 e28dd004 e12fff1e
endmodule

module Register_File (
  input  WriteEnable,
  input  Clock,
  input  Clear,
  input  [3:0] A1,
  input  [3:0] A2,
  input  [3:0] A3,
  input  [31:0] WD3,
  input  [31:0] R15,
  output [31:0] RD1,
  output [31:0] RD2,
  output [31:0] R14,
  output [31:0] R13,
  output [31:0] R12,
  output [31:0] R11,
  output [31:0] R10,
  output [31:0] R9,
  output [31:0] R8,
  output [31:0] R7,
  output [31:0] R6,
  output [31:0] R5,
  output [31:0] R4,
  output [31:0] R3,
  output [31:0] R2,
  output [31:0] R1,
  output [31:0] R0
);

  wire decoder_1_out0, decoder_1_out1, decoder_1_out2, decoder_1_out3, decoder_1_out4, decoder_1_out5,
       decoder_1_out6, decoder_1_out7, decoder_1_out8, decoder_1_out9, decoder_1_out10, decoder_1_out11,
       decoder_1_out12, decoder_1_out13, decoder_1_out14;

  Decoder_part #(.select(4), .disabled(0)) decoder_1 (
    .out0(decoder_1_out0), .out1(decoder_1_out1), .out2(decoder_1_out2), .out3(decoder_1_out3),
    .out4(decoder_1_out4), .out5(decoder_1_out5), .out6(decoder_1_out6), .out7(decoder_1_out7),
    .out8(decoder_1_out8), .out9(decoder_1_out9), .out10(decoder_1_out10), .out11(decoder_1_out11),
    .out12(decoder_1_out12), .out13(decoder_1_out13), .out14(decoder_1_out14), .sel(A3), .en(WriteEnable));  // open: out15
  Register #(.width(32)) u_R14 (.D(WD3), .en(decoder_1_out14), .Q(R14), .clk(Clock), .clr(Clear));
  Register #(.width(32)) u_R13 (.D(WD3), .en(decoder_1_out13), .Q(R13), .clk(Clock), .clr(Clear));
  Register #(.width(32)) u_R12 (.D(WD3), .en(decoder_1_out12), .Q(R12), .clk(Clock), .clr(Clear));
  Register #(.width(32)) u_R11 (.D(WD3), .en(decoder_1_out11), .Q(R11), .clk(Clock), .clr(Clear));
  Register #(.width(32)) u_R10 (.D(WD3), .en(decoder_1_out10), .Q(R10), .clk(Clock), .clr(Clear));
  Register #(.width(32)) u_R9 (.D(WD3), .en(decoder_1_out9), .Q(R9), .clk(Clock), .clr(Clear));
  Register #(.width(32)) u_R8 (.D(WD3), .en(decoder_1_out8), .Q(R8), .clk(Clock), .clr(Clear));
  Register #(.width(32)) u_R7 (.D(WD3), .en(decoder_1_out7), .Q(R7), .clk(Clock), .clr(Clear));
  Register #(.width(32)) u_R6 (.D(WD3), .en(decoder_1_out6), .Q(R6), .clk(Clock), .clr(Clear));
  Register #(.width(32)) u_R5 (.D(WD3), .en(decoder_1_out5), .Q(R5), .clk(Clock), .clr(Clear));
  Register #(.width(32)) u_R4 (.D(WD3), .en(decoder_1_out4), .Q(R4), .clk(Clock), .clr(Clear));
  Register #(.width(32)) u_R3 (.D(WD3), .en(decoder_1_out3), .Q(R3), .clk(Clock), .clr(Clear));
  Register #(.width(32)) u_R2 (.D(WD3), .en(decoder_1_out2), .Q(R2), .clk(Clock), .clr(Clear));
  Register #(.width(32)) u_R1 (.D(WD3), .en(decoder_1_out1), .Q(R1), .clk(Clock), .clr(Clear));
  Register #(.width(32)) u_R0 (.D(WD3), .en(decoder_1_out0), .Q(R0), .clk(Clock), .clr(Clear));
  Multiplexer #(.select(4), .width(32), .disabled(0), .enable("false")) multiplexer_1 (
    .in0(R0), .in1(R1), .in2(R2), .in3(R3), .in4(R4), .in5(R5), .in6(R6), .in7(R7), .in8(R8), .in9(R9),
    .in10(R10), .in11(R11), .in12(R12), .in13(R13), .in14(R14), .in15(R15), .out(RD1), .sel(A1));
  Multiplexer #(.select(4), .width(32), .disabled(0), .enable("false")) multiplexer_2 (
    .in0(R0), .in1(R1), .in2(R2), .in3(R3), .in4(R4), .in5(R5), .in6(R6), .in7(R7), .in8(R8), .in9(R9),
    .in10(R10), .in11(R11), .in12(R12), .in13(R13), .in14(R14), .in15(R15), .out(RD2), .sel(A2));
endmodule

module Data_Memory (
  input  Clock,
  input  WE,
  input  RESET,
  input  [31:0] A,
  input  [31:0] WD,
  output [31:0] RD
);

  wire not_1_out;

  // Probe on A
  // Probe on WD
  not not_1 (not_1_out, WE);
  RAM #(.dataWidth(32), .bus("separate")) ram_1 (
    .addr(A[9:2]), .din(WD), .data(RD), .str(WE), .sel(1'b1), .clk(Clock), .ld(not_1_out), .clr(RESET));
  // Probe on RD
endmodule

module ALU (
  input  [1:0] ALUControll,
  input  [31:0] A,
  input  [31:0] B,
  input  BL,
  input  Bx,
  output [31:0] RESULT,
  output [3:0] Flags
);

  wire adder_1_cout, not_1_out, not_2_out, xnor_1_out, xor_1_out;
  wire [1:0] multiplexer_1_out, multiplexer_2_out;
  wire [31:0] adder_1_out, multiplexer_3_out, multiplexer_4_out, multiplexer_5_out, not_3_out,
       subtractor_1_out;

  Multiplexer #(.width(2), .disabled(0), .enable("false")) multiplexer_1 (
    .in0(ALUControll), .in1(2'b11), .out(multiplexer_1_out), .sel(Bx));
  Multiplexer #(.width(2), .disabled(0), .enable("false")) multiplexer_2 (
    .in0(multiplexer_1_out), .in1(2'b00), .out(multiplexer_2_out), .sel(BL));
  NotExactlyOne xnor_1 (.out(xnor_1_out), .in0(multiplexer_2_out[0]), .in1(A[31]), .in2(B[31]));
  ExactlyOne xor_1 (.out(xor_1_out), .in0(A[31]), .in1(B[31]), .in2(adder_1_out[31]));
  and and_1 (Flags[3], xnor_1_out, xor_1_out, not_1_out);
  not not_1 (not_1_out, multiplexer_2_out[1]);
  and and_2 (Flags[2], not_1_out, adder_1_cout);
  Multiplexer #(.width(32), .disabled(0), .enable("false")) multiplexer_3 (
    .in0(A), .in1(B), .out(multiplexer_3_out), .sel(not_2_out));
  not not_2 (not_2_out, BL);
  ALUHelper aluhelper_1 (.in_1({Flags[1], RESULT[30:0]}), .Zero(Flags[0]));
  // Probe on A
  assign not_3_out = ~B;  // NOT_Gate not_3, 32 bits wide
  Adder #(.width(32)) adder_1 (
    .a(multiplexer_5_out), .b(A), .out(adder_1_out), .cin(multiplexer_2_out[0]), .cout(adder_1_cout));
  Subtractor #(.width(32)) subtractor_1 (.a(A), .b(B), .out(subtractor_1_out));  // open: bin, bout
  Multiplexer #(.width(32), .disabled(0), .enable("false")) multiplexer_4 (
    .in0(multiplexer_3_out), .in1(B), .out(multiplexer_4_out), .sel(Bx));
  // Probe on B
  Multiplexer #(.width(32), .disabled(0)) multiplexer_5 (
    .in0(B), .in1(not_3_out), .out(multiplexer_5_out), .sel(multiplexer_2_out[0]), .en(1'b1));
  Multiplexer #(.select(2), .width(32), .disabled(0)) multiplexer_6 (
    .in0(adder_1_out), .in1(subtractor_1_out), .in2(subtractor_1_out), .in3(multiplexer_4_out),
    .out({Flags[1], RESULT[30:0]}), .sel(multiplexer_2_out), .en(1'b1));
  // Probe on {Flags[1], RESULT[30:0]}

  assign RESULT[31] = Flags[1];
endmodule

module ALUHelper (
  input  [31:0] in_1,
  output Zero
);

  and and_1 (Zero, ~in_1[15], ~in_1[0], ~in_1[1], ~in_1[2], ~in_1[3], ~in_1[4], ~in_1[5], ~in_1[6], ~in_1[7], ~in_1[8], ~in_1[9], ~in_1[10], ~in_1[11], ~in_1[12], ~in_1[13], ~in_1[14], ~in_1[16], ~in_1[17], ~in_1[18], ~in_1[19], ~in_1[20], ~in_1[21], ~in_1[22], ~in_1[23], ~in_1[24], ~in_1[25], ~in_1[26], ~in_1[27], ~in_1[28], ~in_1[29], ~in_1[30], ~in_1[31]);  // AND_Gate
endmodule

module Control_Unit (
  input  Clock,
  input  [31:0] Instruction_word,
  input  [3:0] ALUFlags,
  output MemtoReg,
  output ALUSrc,
  output [1:0] ImmedSrc,
  output [2:0] RegSrc,
  output [1:0] ALUControl,
  output PCSrc,
  output RegW,
  output MemW,
  output FlagWrite,
  output BX
);

  wire decoder_1_memw, decoder_1_pcsrc, decoder_1_regw;

  Decoder decoder_1 (
    .IW(Instruction_word), .PcSrc(decoder_1_pcsrc), .MemtoReg(MemtoReg), .MemW(decoder_1_memw),
    .ALUSrc(ALUSrc), .ImmSrc(ImmedSrc), .RegW(decoder_1_regw), .RegSrc(RegSrc), .ALUControl(ALUControl),
    .FlagW(FlagWrite), .BX(BX));
  Conditional_Logic conditional_logic_1 (
    .FlagW(FlagWrite), .PCSrc(decoder_1_pcsrc), .RegW(decoder_1_regw), .MemW(decoder_1_memw),
    .Cond(Instruction_word[31:28]), .ALUFlags(ALUFlags), .Clock(Clock), .PCSrc_2(PCSrc), .RegWrite(RegW),
    .MemWrite(MemW));
endmodule

module PC (
  input  [31:0] D,
  input  Clear,
  input  Clock,
  output [31:0] Output
);

  Register #(.width(32)) register_1 (.D(D), .en(1'b1), .Q(Output), .clk(Clock), .clr(Clear));
endmodule

module Inst_Word (
  input  [31:0] IW,
  output [31:0] IW_2,
  output [3:0] _19_16,
  output [3:0] _3_0,
  output [3:0] _15_12,
  output [23:0] _23_0
);


  assign _3_0 = IW[3:0];
  assign _15_12 = IW[15:12];
  assign _19_16 = IW[19:16];
  assign _23_0 = IW[23:0];
  assign IW_2 = IW;
endmodule

module Extender (
  input  [1:0] in_1,
  input  [23:0] Input,
  output [31:0] Output
);

  wire [23:0] shifter_1_out;
  wire [31:0] bit_extender_1_out, bit_extender_2_out, bit_extender_3_out;

  // Probe on Input
  assign bit_extender_1_out = {{24{1'b0}}, Input[7:0]};  // Bit_Extender bit_extender_1
  assign bit_extender_2_out = {{20{1'b0}}, Input[11:0]};  // Bit_Extender bit_extender_2
  Shifter #(.width(24)) shifter_1 (.in(Input), .\dist (5'b00010), .out(shifter_1_out));
  assign bit_extender_3_out = {{8{shifter_1_out[23]}}, shifter_1_out};  // Bit_Extender bit_extender_3
  Multiplexer #(.select(2), .width(32), .disabled(0), .enable("false")) multiplexer_1 (
    .in0(bit_extender_1_out), .in1(bit_extender_2_out), .in2(bit_extender_3_out), .out(Output), .sel(in_1));  // open: in3
  // Probe on Output
endmodule

module Decoder (
  input  [31:0] IW,
  output PcSrc,
  output MemtoReg,
  output MemW,
  output ALUSrc,
  output [1:0] ImmSrc,
  output RegW,
  output [2:0] RegSrc,
  output [1:0] ALUControl,
  output FlagW,
  output BX
);

  wire and_1_out, and_2_out, maindecoder_1_aluop, maindecoder_1_branch, pclogic_1_pcsrc;
  wire [1:0] aludecoder_1_alucontrol;

  MainDecoder maindecoder_1 (
    .Funct_5_0(IW[25:20]), .Op_1_0(IW[27:26]), ._24(IW[27:4]), .Branch(maindecoder_1_branch),
    .MemtoReg(MemtoReg), .MemW(MemW), .ALUSrc(ALUSrc), .ImmSrc(ImmSrc), .RegW(RegW), .RegSrc(RegSrc),
    .ALUOp(maindecoder_1_aluop), .BX(BX));
  ALUDecoder aludecoder_1 (
    ._4_0_Funct(IW[24:21]), .ALuOP(maindecoder_1_aluop), .ALUControl(aludecoder_1_alucontrol), .FlagW(FlagW));
  and and_1 (and_1_out, ~IW[26], IW[27]);  // AND_Gate
  PCLogic pclogic_1 (.Rd(IW[15:12]), .RegWrite(RegW), .B(maindecoder_1_branch), .PCSrc(pclogic_1_pcsrc));
  and and_2 (and_2_out, and_1_out, IW[24]);
  Multiplexer #(.width(2), .disabled(0), .enable("false")) multiplexer_1 (
    .in0(aludecoder_1_alucontrol), .in1(2'b11), .out(ALUControl), .sel(and_2_out));
  Multiplexer #(.disabled(0), .enable("false")) multiplexer_2 (
    .in0(pclogic_1_pcsrc), .in1(1'b1), .out(PcSrc), .sel(BX));

  // Notes on the sheet:
  //   Cond
  //   rd
  //   Op
  //   funct
endmodule

module ALUDecoder (
  input  ALuOP,
  input  [3:0] _4_0_Funct,
  output [1:0] ALUControl,
  output FlagW
);

  wire decoder_1_out0, decoder_1_out2, decoder_1_out4, decoder_1_out13, decoder_1_out15;

  Decoder_part #(.select(4), .disabled(0), .enable("false")) decoder_1 (
    .out0(decoder_1_out0), .out2(decoder_1_out2), .out4(decoder_1_out4), .out10(FlagW),
    .out13(decoder_1_out13), .out15(decoder_1_out15), .sel(_4_0_Funct));  // open: out1, out3, out5, out6, out7, out8, out9, out11, out12, out14
  or or_1 (ALUControl[0], decoder_1_out2, decoder_1_out13, decoder_1_out15);
  or or_2 (ALUControl[1], FlagW, decoder_1_out13);

  // Notes on the sheet:
  //   and
  //   sub
  //   Add
  //   cmp
  //   mov
endmodule

module MainDecoder (
  input  [5:0] Funct_5_0,
  input  [1:0] Op_1_0,
  input  [23:0] _24,
  output Branch,
  output MemtoReg,
  output MemW,
  output ALUSrc,
  output [1:0] ImmSrc,
  output RegW,
  output [2:0] RegSrc,
  output ALUOp,
  output BX
);

  wire and_1_out, and_3_out, comparator_2_eq, comparator_3_eq, DP_Immd_out, DP_Reg_out, not_1_out, or_3_out,
       or_4_out;

  Comparator #(.width(24), .mode("unsigned")) comparator_1 (.a(_24), .b(24'h12fff1), .eq(BX));  // open: gt, lt
  and DP_Reg (DP_Reg_out, ~Op_1_0[1], ~Op_1_0[0], ~Funct_5_0[5], ~BX);  // AND_Gate
  and DP_Immd (DP_Immd_out, ~Op_1_0[1], ~Op_1_0[0], Funct_5_0[5], ~BX);  // AND_Gate
  and STR (MemW, ~Op_1_0[1], Op_1_0[0], ~Funct_5_0[0], ~BX);  // AND_Gate
  and LDR (MemtoReg, ~Op_1_0[1], Op_1_0[0], Funct_5_0[0], ~BX);  // AND_Gate
  and B (Branch, Op_1_0[1], ~Op_1_0[0]);  // AND_Gate
  and BL (RegSrc[2], Op_1_0[1], ~Op_1_0[0], Funct_5_0[4]);  // AND_Gate
  Comparator #(.width(4), .mode("unsigned")) comparator_2 (
    .a(4'b1010), .b(Funct_5_0[4:1]), .eq(comparator_2_eq));  // open: gt, lt
  or or_1 (ALUSrc, DP_Immd_out, MemW, MemtoReg, Branch);
  or or_2 (ImmSrc[0], MemW, MemtoReg);
  or or_3 (or_3_out, DP_Reg_out, DP_Immd_out, MemtoReg);
  or or_4 (or_4_out, DP_Reg_out, DP_Immd_out);
  and and_1 (and_1_out, or_3_out, not_1_out);
  not not_1 (not_1_out, comparator_2_eq);
  and and_2 (ALUOp, or_4_out, ~BX);  // AND_Gate
  Comparator #(.width(24), .mode("unsigned")) comparator_3 (
    .a(_24), .b({24{1'b0}}), .eq(comparator_3_eq));  // open: gt, lt
  and and_3 (and_3_out, and_1_out, ~comparator_3_eq);  // AND_Gate
  or or_5 (RegW, and_3_out, RegSrc[2]);

  assign ImmSrc[1] = Branch;
  assign RegSrc[1:0] = {MemW, Branch};

  // Notes on the sheet:
  //   op1
  //   Op0
  //   f0
  //   f5
  //   Bx
endmodule

module PCLogic (
  input  [3:0] Rd,
  input  RegWrite,
  input  B,
  output PCSrc
);

  wire and_1_out, comparator_1_eq;

  Comparator #(.width(4), .mode("unsigned")) comparator_1 (.a(4'b1111), .b(Rd), .eq(comparator_1_eq));  // open: gt, lt
  and and_1 (and_1_out, comparator_1_eq, RegWrite);
  or or_1 (PCSrc, and_1_out, B);
endmodule

module Conditional_Logic (
  input  Clock,
  input  FlagW,
  input  PCSrc,
  input  RegW,
  input  MemW,
  input  [3:0] Cond,
  input  [3:0] ALUFlags,
  output PCSrc_2,
  output RegWrite,
  output MemWrite
);

  wire and_1_out, cond_check_1_condexe;
  wire [1:0] register_1_q, register_2_q;

  Register #(.width(2)) register_1 (.D(ALUFlags[3:2]), .en(and_1_out), .Q(register_1_q), .clk(Clock));  // open: clr
  Register #(.width(2)) register_2 (.D(ALUFlags[1:0]), .en(and_1_out), .Q(register_2_q), .clk(Clock));  // open: clr
  and and_1 (and_1_out, FlagW, cond_check_1_condexe);
  Cond_Check cond_check_1 (
    .Flags_3_2__VC(register_1_q), .Flags_1_0__NZ(register_2_q), .Cond(Cond), .CondExe(cond_check_1_condexe));
  and and_2 (PCSrc_2, PCSrc, cond_check_1_condexe);
  and and_3 (RegWrite, RegW, cond_check_1_condexe);
  and and_4 (MemWrite, MemW, cond_check_1_condexe);

  // Other names for the same wires on the sheet: CLK = Clock
endmodule

module Cond_Check (
  input  [3:0] Cond,
  input  [1:0] Flags_3_2__VC,
  input  [1:0] Flags_1_0__NZ,
  output CondExe
);

  wire AL_out, and_1_out, and_2_out, and_3_out, EQ_out, GT_2_out, GT_out, LT_2_out, LT_out, NE_out,
       xor_1_out, xor_2_out;

  and and_1 (and_1_out, ~Cond[0], ~Cond[1], ~Cond[2], ~Cond[3]);  // AND_Gate
  and EQ (EQ_out, and_1_out, Flags_1_0__NZ[0]);
  and and_2 (and_2_out, Cond[0], ~Cond[1], ~Cond[2], ~Cond[3]);  // AND_Gate
  and and_3 (and_3_out, ~Flags_1_0__NZ[0], ~xor_1_out);  // AND_Gate
  xor xor_1 (xor_1_out, Flags_1_0__NZ[1], Flags_3_2__VC[1]);
  and GT (GT_out, ~Cond[0], ~Cond[1], Cond[2], Cond[3]);  // AND_Gate
  xor xor_2 (xor_2_out, Flags_1_0__NZ[1], Flags_3_2__VC[1]);
  and LT (LT_out, Cond[0], Cond[1], ~Cond[2], Cond[3]);  // AND_Gate
  and AL (AL_out, ~Cond[0], Cond[1], Cond[2], Cond[3]);  // AND_Gate
  and NE (NE_out, ~Flags_1_0__NZ[0], and_2_out);  // AND_Gate
  and GT_2 (GT_2_out, and_3_out, GT_out);
  and LT_2 (LT_2_out, xor_2_out, LT_out);
  or or_1 (CondExe, EQ_out, NE_out, GT_2_out, LT_2_out, AL_out);

  // Other names for the same wires on the sheet: C0 = Cond[0]; C1 = Cond[1]; C2 = Cond[2]; C3 = Cond[3]
endmodule
